// Digital circuit Demux_1entrie_4outs.dig as structural Verilog
module Demux_1entrie_4outs (
  input  Sel2,
  input  Input,
  input  Sel1,
  output Ouput0,
  output Output1,
  output Output2,
  output Output3
);

  wire not_1_out, not_2_out;

  not not_1 (not_1_out, Sel2);
  not not_2 (not_2_out, Sel1);
  and and_1 (Ouput0, Input, not_1_out, not_2_out);
  and and_2 (Output1, Input, Sel1, not_1_out);
  and and_3 (Output2, not_2_out, Sel2, Input);
  and and_4 (Output3, Sel1, Sel2, Input);

  // Notes on the sheet:
  //   Usamos compuertas lógicas AND de 3 entradas,
  //   para poder utilizar 3 inputs, 2 inputs para 
  //   seleccionar la salida, y uno para representar la
  //   señal de entrada del Demux
  //   Demux 1input 4outputs
  //   Utilizamos dos botones de input para representar
  //   dos bits de entrada, que permiten tener 4 combinaciones
  //   para seleccionar cada una de las salidas del Demux
endmodule
