// Digital circuit GPIO_Port.dig as structural Verilog
module GPIO_Port (
  input  Set,
  input  Clear,
  input  Set_2,
  input  Enable,
  input  Clear_2,
  input  I_0_PA0,
  input  Channel_PA0,
  input  Set_3,
  input  Clear_3,
  input  Output_PA3,
  input  Output_PA2,
  input  Output_PA0,
  input  Output_PA1,
  input  Input,
  input  I_0_PA1,
  input  Channel_PA1,
  input  I_0_PA2,
  input  Channel_PA2,
  input  I_0_PA3,
  input  Channel_PA3,
  input  Set_4,
  input  Clear_4,
  input  Set_5,
  input  Clear_5,
  input  Alt_PA3,
  input  Alt_PA2,
  input  Alt_PA0,
  input  Alt_PA1,
  input  Clock,
  input  Clock_Manual,
  input  Input_2,
  input  Input_3,
  input  Input_4,
  output out_1,
  output out_2,
  output out_3,
  output out_4,
  output out_18,
  output out_26,
  output out_27,
  output out_28,
  output out_29,
  output out_40,
  output out_42,
  output out_44
);

  wire driver_1_out, driver_2_out, driver_3_out, driver_4_out, driverinvsel_2_out, driverinvsel_4_out,
       driverinvsel_6_out, driverinvsel_8_out, driverinvsel_9_out, driverinvsel_10_out, driverinvsel_11_out,
       driverinvsel_12_out, multiplexer_1_out, multiplexer_2_out, multiplexer_3_out, multiplexer_4_out,
       multiplexer_5_out, multiplexer_6_out, multiplexer_7_out, multiplexer_8_out, multiplexer_9_out,
       multiplexer_10_out, multiplexer_11_out, multiplexer_12_out, multiplexer_13_out, multiplexer_14_out,
       multiplexer_15_out, multiplexer_16_out, multiplexer_17_out, multiplexer_18_out, multiplexer_19_out,
       multiplexer_20_out, multiplexer_21_out, multiplexer_22_out, multiplexer_23_out, multiplexer_24_out,
       PA0_AltOut, PA0_Analog, PA0_Cha, PA0_I_O, PA0_Input, PA0_Out, PA1_AltOut, PA1_Analog, PA1_Cha,
       PA1_I_O, PA1_Input, PA1_Out, PA2_AltOut, PA2_Analog, PA2_Cha, PA2_I_O, PA2_Input, PA2_Out, PA3_AltOut,
       PA3_Analog, PA3_Cha, PA3_I_O, PA3_Input, PA3_Out, PA_Cha_0, PA_Cha_1, PA_I_O_0, PA_I_O_1;

  Multiplexer multiplexer_1 (.sel(Enable), .in_0(PA3_Cha), .in_1(Channel_PA3), .out(multiplexer_1_out));
  D_FF_AS d_ff_as_1 (.Set(Set_2), .D(multiplexer_1_out), .C(Clock), .Clr(Clear_2), .Q(PA3_Cha));  // open: nQ
  Multiplexer multiplexer_2 (.sel(Enable), .in_0(PA3_I_O), .in_1(I_0_PA3), .out(multiplexer_2_out));
  D_FF_AS d_ff_as_2 (.Set(Set_2), .D(multiplexer_2_out), .C(Clock), .Clr(Clear_2), .Q(PA3_I_O));  // open: nQ
  Multiplexer multiplexer_3 (.sel(Enable), .in_0(PA2_Cha), .in_1(Channel_PA2), .out(multiplexer_3_out));
  nand nand_1 (PA_I_O_0, PA0_I_O, PA1_I_O, PA2_I_O, PA3_I_O);
  or or_1 (PA_I_O_1, PA0_I_O, PA1_I_O, PA2_I_O, PA3_I_O);
  nand nand_2 (PA_Cha_0, PA0_Cha, PA1_Cha, PA2_Cha, PA3_Cha);
  or or_2 (PA_Cha_1, PA0_Cha, PA1_Cha, PA2_Cha, PA3_Cha);
  D_FF_AS d_ff_as_3 (.Set(Set_2), .D(multiplexer_3_out), .C(Clock), .Clr(Clear_2), .Q(PA2_Cha));  // open: nQ
  Multiplexer multiplexer_4 (.sel(Enable), .in_0(PA2_I_O), .in_1(I_0_PA2), .out(multiplexer_4_out));
  D_FF_AS d_ff_as_4 (.Set(Set_2), .D(multiplexer_4_out), .C(Clock), .Clr(Clear_2), .Q(PA2_I_O));  // open: nQ
  assign driver_1_out = PA_I_O_0 ? PA_Cha_0 : 1'bz;  // Driver driver_1
  assign driver_2_out = PA_I_O_0 ? PA_Cha_1 : 1'bz;  // Driver driver_2
  Multiplexer multiplexer_5 (.sel(Enable), .in_0(PA1_Cha), .in_1(Channel_PA1), .out(multiplexer_5_out));
  assign driver_3_out = PA_I_O_1 ? PA_Cha_0 : 1'bz;  // Driver driver_3
  assign driver_4_out = PA_I_O_1 ? PA_Cha_1 : 1'bz;  // Driver driver_4
  Multiplexer multiplexer_6 (.sel(driver_1_out), .in_0(out_1), .in_1(PA3_Input), .out(multiplexer_6_out));
  Multiplexer multiplexer_7 (.sel(driver_2_out), .in_0(out_26), .in_1(PA3_Analog), .out(multiplexer_7_out));
  Multiplexer multiplexer_8 (.sel(driver_3_out), .in_0(PA3_Out), .in_1(Output_PA3), .out(multiplexer_8_out));
  Multiplexer multiplexer_9 (.sel(driver_4_out), .in_0(PA3_AltOut), .in_1(Alt_PA3), .out(multiplexer_9_out));
  D_FF_AS d_ff_as_5 (.Set(Set_2), .D(multiplexer_5_out), .C(Clock), .Clr(Clear_2), .Q(PA1_Cha));  // open: nQ
  D_FF_AS d_ff_as_6 (.Set(Set), .D(multiplexer_6_out), .C(Clock), .Clr(Clear), .Q(out_1));  // open: nQ
  D_FF_AS d_ff_as_7 (.Set(Set_4), .D(multiplexer_7_out), .C(Clock), .Clr(Clear_4), .Q(out_26));  // open: nQ
  D_FF_AS d_ff_as_8 (.Set(Set_3), .D(multiplexer_8_out), .C(Clock), .Clr(Clear_3), .Q(PA3_Out));  // open: nQ
  D_FF_AS d_ff_as_9 (.Set(Set_5), .D(multiplexer_9_out), .C(Clock), .Clr(Clear_5), .Q(PA3_AltOut));  // open: nQ
  Multiplexer multiplexer_10 (.sel(Enable), .in_0(PA1_I_O), .in_1(I_0_PA1), .out(multiplexer_10_out));
  Multiplexer multiplexer_11 (.sel(driver_1_out), .in_0(out_2), .in_1(PA2_Input), .out(multiplexer_11_out));
  Multiplexer multiplexer_12 (.sel(driver_2_out), .in_0(out_27), .in_1(PA2_Analog), .out(multiplexer_12_out));
  Multiplexer multiplexer_13 (.sel(driver_3_out), .in_0(PA2_Out), .in_1(Output_PA2), .out(multiplexer_13_out));
  Multiplexer multiplexer_14 (.sel(driver_4_out), .in_0(PA2_AltOut), .in_1(Alt_PA2), .out(multiplexer_14_out));
  D_FF_AS d_ff_as_10 (.Set(Set_2), .D(multiplexer_10_out), .C(Clock), .Clr(Clear_2), .Q(PA1_I_O));  // open: nQ
  D_FF_AS d_ff_as_11 (.Set(Set), .D(multiplexer_11_out), .C(Clock), .Clr(Clear), .Q(out_2));  // open: nQ
  D_FF_AS d_ff_as_12 (.Set(Set_4), .D(multiplexer_12_out), .C(Clock), .Clr(Clear_4), .Q(out_27));  // open: nQ
  D_FF_AS d_ff_as_13 (.Set(Set_3), .D(multiplexer_13_out), .C(Clock), .Clr(Clear_3), .Q(PA2_Out));  // open: nQ
  D_FF_AS d_ff_as_14 (.Set(Set_5), .D(multiplexer_14_out), .C(Clock), .Clr(Clear_5), .Q(PA2_AltOut));  // open: nQ
  Multiplexer multiplexer_15 (.sel(Enable), .in_0(PA0_Cha), .in_1(Channel_PA0), .out(multiplexer_15_out));
  Multiplexer multiplexer_16 (.sel(driver_1_out), .in_0(out_3), .in_1(PA1_Input), .out(multiplexer_16_out));
  Multiplexer multiplexer_17 (.sel(driver_2_out), .in_0(out_28), .in_1(PA1_Analog), .out(multiplexer_17_out));
  Multiplexer multiplexer_18 (.sel(driver_3_out), .in_0(PA1_Out), .in_1(Output_PA1), .out(multiplexer_18_out));
  Multiplexer multiplexer_19 (.sel(driver_4_out), .in_0(PA1_AltOut), .in_1(Alt_PA1), .out(multiplexer_19_out));
  D_FF_AS d_ff_as_15 (.Set(Set), .D(multiplexer_16_out), .C(Clock), .Clr(Clear), .Q(out_3));  // open: nQ
  D_FF_AS d_ff_as_16 (.Set(Set_4), .D(multiplexer_17_out), .C(Clock), .Clr(Clear_4), .Q(out_28));  // open: nQ
  D_FF_AS d_ff_as_17 (.Set(Set_2), .D(multiplexer_15_out), .C(Clock), .Clr(Clear_2), .Q(PA0_Cha));  // open: nQ
  D_FF_AS d_ff_as_18 (.Set(Set_3), .D(multiplexer_18_out), .C(Clock), .Clr(Clear_3), .Q(PA1_Out));  // open: nQ
  D_FF_AS d_ff_as_19 (.Set(Set_5), .D(multiplexer_19_out), .C(Clock), .Clr(Clear_5), .Q(PA1_AltOut));  // open: nQ
  Multiplexer multiplexer_20 (.sel(Enable), .in_0(PA0_I_O), .in_1(I_0_PA0), .out(multiplexer_20_out));
  Multiplexer multiplexer_21 (.sel(driver_1_out), .in_0(out_4), .in_1(PA0_Input), .out(multiplexer_21_out));
  Multiplexer multiplexer_22 (.sel(driver_2_out), .in_0(out_29), .in_1(PA0_Analog), .out(multiplexer_22_out));
  Multiplexer multiplexer_23 (.sel(driver_3_out), .in_0(PA0_Out), .in_1(Output_PA0), .out(multiplexer_23_out));
  Multiplexer multiplexer_24 (.sel(driver_4_out), .in_0(PA0_AltOut), .in_1(Alt_PA0), .out(multiplexer_24_out));
  D_FF_AS d_ff_as_20 (.Set(Set), .D(multiplexer_21_out), .C(Clock), .Clr(Clear), .Q(out_4));  // open: nQ
  D_FF_AS d_ff_as_21 (.Set(Set_4), .D(multiplexer_22_out), .C(Clock), .Clr(Clear_4), .Q(out_29));  // open: nQ
  D_FF_AS d_ff_as_22 (.Set(Set_2), .D(multiplexer_20_out), .C(Clock), .Clr(Clear_2), .Q(PA0_I_O));  // open: nQ
  D_FF_AS d_ff_as_23 (.Set(Set_3), .D(multiplexer_23_out), .C(Clock), .Clr(Clear_3), .Q(PA0_Out));  // open: nQ
  D_FF_AS d_ff_as_24 (.Set(Set_5), .D(multiplexer_24_out), .C(Clock), .Clr(Clear_5), .Q(PA0_AltOut));  // open: nQ
  assign PA0_Input = ~PA0_Cha ? driverinvsel_9_out : 1'bz;  // DriverInvSel driverinvsel_1
  assign PA0_Analog = PA0_Cha ? driverinvsel_9_out : 1'bz;  // Driver driver_5
  assign driverinvsel_2_out = ~PA0_Cha ? PA0_Out : 1'bz;  // DriverInvSel driverinvsel_2
  assign driverinvsel_2_out = PA0_Cha ? PA0_AltOut : 1'bz;  // Driver driver_6
  assign PA1_Input = ~PA1_Cha ? driverinvsel_10_out : 1'bz;  // DriverInvSel driverinvsel_3
  assign PA1_Analog = PA1_Cha ? driverinvsel_10_out : 1'bz;  // Driver driver_7
  assign driverinvsel_4_out = ~PA1_Cha ? PA1_Out : 1'bz;  // DriverInvSel driverinvsel_4
  assign driverinvsel_4_out = PA1_Cha ? PA1_AltOut : 1'bz;  // Driver driver_8
  assign PA2_Input = ~PA2_Cha ? driverinvsel_11_out : 1'bz;  // DriverInvSel driverinvsel_5
  assign PA2_Analog = PA2_Cha ? driverinvsel_11_out : 1'bz;  // Driver driver_9
  assign driverinvsel_6_out = ~PA2_Cha ? PA2_Out : 1'bz;  // DriverInvSel driverinvsel_6
  assign driverinvsel_6_out = PA2_Cha ? PA2_AltOut : 1'bz;  // Driver driver_10
  assign PA3_Input = ~PA3_Cha ? driverinvsel_12_out : 1'bz;  // DriverInvSel driverinvsel_7
  assign PA3_Analog = PA3_Cha ? driverinvsel_12_out : 1'bz;  // Driver driver_11
  assign driverinvsel_8_out = ~PA3_Cha ? PA3_Out : 1'bz;  // DriverInvSel driverinvsel_8
  assign driverinvsel_8_out = PA3_Cha ? PA3_AltOut : 1'bz;  // Driver driver_12
  assign driverinvsel_9_out = ~PA0_I_O ? Input : 1'bz;  // DriverInvSel driverinvsel_9
  assign out_18 = PA0_I_O ? driverinvsel_2_out : 1'bz;  // Driver driver_13
  assign driverinvsel_10_out = ~PA1_I_O ? Input_2 : 1'bz;  // DriverInvSel driverinvsel_10
  assign out_40 = PA1_I_O ? driverinvsel_4_out : 1'bz;  // Driver driver_14
  assign driverinvsel_11_out = ~PA2_I_O ? Input_3 : 1'bz;  // DriverInvSel driverinvsel_11
  assign out_42 = PA2_I_O ? driverinvsel_6_out : 1'bz;  // Driver driver_15
  assign driverinvsel_12_out = ~PA3_I_O ? Input_4 : 1'bz;  // DriverInvSel driverinvsel_12
  assign out_44 = PA3_I_O ? driverinvsel_8_out : 1'bz;  // Driver driver_16

  // Notes on the sheet:
  //   Estos canales permiten que se activen los diferentes registros del
  //   puerto automaticamente, siempre que haya al menos un pin
  //   utilizando dicho register, de acuerdo a lo almacenado en el 
  //   Operating Mode Register
  //   El Operating Mode Register es un registro de 8 bits
  //   que almacena en 2 bits, la configuración para cada
  //   pin. Dicha configuración permite establecer el tipo de
  //   funcionamiento de cada pin (Input-Output), y de estos
  //   dos modos, permite seleccionar en cual registro se 
  //   almacenará o se accedera a la información.
  //   Los Output Data Register y Alternate Data Register son registros de 4 bits
  //   que envían valores de salida de acuerdo a valores almacenados previamente
  //   en los registros, y además se seleccionan desde el Operating Mode Register.
  //   Operating Mode Register
  //   Los Input Data Register y ADC Input Register son registros de 4 bits que
  //   permiten almacenar datos de entrada de cualquiera de los 4 pines, de 
  //   acuerdo a la configuración del Operating Mode Register.
  //   Input Data Register
  //   ADC Input Register
  //   Output Data Register
  //   Alternate Data Register
  //   El Operating Mode Register cuenta con 2 bits por cada PIN:
  //   - El primer bit (I/0) se encarga de indicar si el PIN es una entrada
  //   o una salida:
  //   0=Input
  //   1=Output
  //   - El segundo bit (Channel) del PIN selecciona el canal activo según 
  //   esté habilitado el modo de entrada o salida:
  //   - Para las entradas:
  //   0=Simple Input
  //   1=Analogic Input
  //   - Para las salidas:
  //   0=Output
  //   1=Alternate
  //   PA0 (PIN)
  //   PA1 (PIN)
  //   PA2 (PIN)
  //   PA3 (PIN)
  //   Demux 2:1
  //   Mux 2:1
endmodule
