// Digital circuit Mux_2entries.dig as structural Verilog
module Mux_2entries (
  input  Input_1,
  input  Input_0,
  input  Sel,
  input  Enable,
  input  Input_T1,
  input  Input_T0,
  input  Input_Gen_1,
  input  Input_Gen_0,
  input  Sel_2,
  output Output,
  output Output_T0,
  output Output_Gen
);

  wire and_1_out, and_2_out, nand_1_out, nand_2_out, not_1_out, not_2_out, not_3_out, not_4_out;

  not not_1 (not_1_out, Input_T0);
  not not_2 (not_2_out, Enable);
  not not_3 (not_3_out, Input_T1);
  nand nand_1 (nand_1_out, not_2_out, Input_T0);
  and and_1 (and_1_out, not_2_out, not_1_out);
  nand nand_2 (nand_2_out, Enable, Input_T1);
  and and_2 (and_2_out, Enable, not_3_out);
  PFET pfet_1 (.G(nand_1_out), .S(1'b1), .D(Output_T0));
  NFET nfet_1 (.G(and_1_out), .D(Output_T0), .S(1'b0));
  PFET pfet_2 (.G(nand_2_out), .S(1'b1), .D(Output_T0));
  NFET nfet_2 (.G(and_2_out), .D(Output_T0), .S(1'b0));
  not not_4 (not_4_out, Sel);
  Multiplexer multiplexer_1 (.sel(Sel_2), .in_0(Input_Gen_0), .in_1(Input_Gen_1), .out(Output_Gen));
  assign Output = not_4_out ? Input_0 : 1'bz;  // Driver driver_1
  assign Output = Sel ? Input_1 : 1'bz;  // Driver driver_2

  // Notes on the sheet:
  //   Creamos un Mux de dos entradas con dos BufferTristate.
  //   El input del Enable junto con la negación hacia uno de los
  //   Buffers, permite tener activado siempre uno de los dos 
  //   Buffers, podiendo así obtener una valor siempre a la salida.
  //   Mux Test
  //   Mux 2entries
  //   Mux 2:1 Generic
endmodule
